// Logisim project FixedPointALU.circ as structural Verilog: 16 circuits, main circuit ALU
module ALU (
  input  A0,
  input  A1,
  input  A2,
  input  A3,
  input  A4,
  input  A5,
  input  A6,
  input  A7,
  input  B0,
  input  B1,
  input  B2,
  input  B3,
  input  B4,
  input  B5,
  input  B6,
  input  B7,
  input  S0,
  input  S1,
  input  S2,
  input  SUB,
  output Z0,
  output Z1,
  output Z2,
  output Z3,
  output Z4,
  output Z5,
  output Z6,
  output Z7,
  output OVERFLOW
);

  wire alu_arithmetic_1_overflow, alu_arithmetic_1_z0, alu_arithmetic_1_z1, alu_arithmetic_1_z2,
       alu_arithmetic_1_z3, alu_arithmetic_1_z4, alu_arithmetic_1_z5, alu_arithmetic_1_z6,
       alu_arithmetic_1_z7, alu_logic_1_z0, alu_logic_1_z1, alu_logic_1_z2, alu_logic_1_z3, alu_logic_1_z4,
       alu_logic_1_z5, alu_logic_1_z6, alu_logic_1_z7;

  ALU_Logic alu_logic_1 (
    .A0(A0), .A1(A1), .A2(A2), .A3(A3), .A4(A4), .A5(A5), .A6(A6), .A7(A7), .B0(B0), .B1(B1), .B2(B2),
    .B3(B3), .B4(B4), .B5(B5), .B6(B6), .B7(B7), .S0(S0), .S1(S1), .Z0(alu_logic_1_z0), .Z1(alu_logic_1_z1),
    .Z2(alu_logic_1_z2), .Z3(alu_logic_1_z3), .Z4(alu_logic_1_z4), .Z5(alu_logic_1_z5), .Z6(alu_logic_1_z6),
    .Z7(alu_logic_1_z7));
  ALU_Arithmetic alu_arithmetic_1 (
    .A0(A0), .A1(A1), .A2(A2), .A3(A3), .A4(A4), .A5(A5), .A6(A6), .A7(A7), .B0(B0), .B1(B1), .B2(B2),
    .B3(B3), .B4(B4), .B5(B5), .B6(B6), .B7(B7), .SUB(SUB), .S0(S0), .S1(S1), .Z0(alu_arithmetic_1_z0),
    .Z1(alu_arithmetic_1_z1), .Z2(alu_arithmetic_1_z2), .Z3(alu_arithmetic_1_z3), .Z4(alu_arithmetic_1_z4),
    .Z5(alu_arithmetic_1_z5), .Z6(alu_arithmetic_1_z6), .Z7(alu_arithmetic_1_z7),
    .OVERFLOW(alu_arithmetic_1_overflow));
  and and_1 (OVERFLOW, S2, alu_arithmetic_1_overflow);
  ALU_MultiplexerX2 alu_multiplexerx2_1 (.S3(S2), .D0(alu_logic_1_z0), .D1(alu_arithmetic_1_z0), .Z(Z0));
  ALU_MultiplexerX2 alu_multiplexerx2_2 (.S3(S2), .D0(alu_logic_1_z1), .D1(alu_arithmetic_1_z1), .Z(Z1));
  ALU_MultiplexerX2 alu_multiplexerx2_3 (.S3(S2), .D0(alu_logic_1_z2), .D1(alu_arithmetic_1_z2), .Z(Z2));
  ALU_MultiplexerX2 alu_multiplexerx2_4 (.S3(S2), .D0(alu_logic_1_z3), .D1(alu_arithmetic_1_z3), .Z(Z3));
  ALU_MultiplexerX2 alu_multiplexerx2_5 (.S3(S2), .D0(alu_logic_1_z4), .D1(alu_arithmetic_1_z4), .Z(Z4));
  ALU_MultiplexerX2 alu_multiplexerx2_6 (.S3(S2), .D0(alu_logic_1_z5), .D1(alu_arithmetic_1_z5), .Z(Z5));
  ALU_MultiplexerX2 alu_multiplexerx2_7 (.S3(S2), .D0(alu_logic_1_z6), .D1(alu_arithmetic_1_z6), .Z(Z6));
  ALU_MultiplexerX2 alu_multiplexerx2_8 (.S3(S2), .D0(alu_logic_1_z7), .D1(alu_arithmetic_1_z7), .Z(Z7));

  // Notes on the sheet:
  //   ADD = 0
  //   SUB =1 
  //   NOT = 000
  //   AND = 010
  //   OR = 100
  //   XOR = 110
  //   ADD/SUB = 001
  //   MULTI = 011
  //   DIV = 101
endmodule

module ALU_MultiplexerX4 (
  input  S0,
  input  S1,
  input  D0,
  input  D1,
  input  D2,
  input  D3,
  output Z
);

  wire and_1_out, and_2_out, and_3_out, and_4_out, not_1_out, not_2_out, not_3_out, not_4_out;

  not not_1 (not_1_out, S0);
  not not_2 (not_2_out, S1);
  not not_3 (not_3_out, S0);
  not not_4 (not_4_out, S1);
  and and_1 (and_1_out, not_1_out, not_2_out, D0);
  and and_2 (and_2_out, not_3_out, S1, D1);
  and and_3 (and_3_out, S0, not_4_out, D2);
  and and_4 (and_4_out, S0, S1, D3);
  or or_1 (Z, and_1_out, and_2_out, and_3_out, and_4_out);
endmodule

module ARITHMETIC_AdderSubtractor (
  input  SUB,
  input  A0,
  input  A1,
  input  A2,
  input  A3,
  input  A4,
  input  A5,
  input  A6,
  input  A7,
  input  B0,
  input  B1,
  input  B2,
  input  B3,
  input  B4,
  input  B5,
  input  B6,
  input  B7,
  output Z0,
  output Z1,
  output Z2,
  output Z3,
  output Z4,
  output Z5,
  output Z6,
  output Z7,
  output OVERFLOW
);

  wire and_1_out, and_2_out, and_3_out, and_4_out, and_5_out, and_6_out, and_7_out, and_8_out, and_9_out,
       and_10_out, and_11_out, and_12_out, and_13_out, and_14_out, and_15_out, and_16_out, not_1_out,
       not_2_out, not_3_out, or_1_out, or_2_out, or_3_out, or_4_out, or_5_out, or_6_out, or_7_out, xor_1_out,
       xor_2_out, xor_3_out, xor_4_out, xor_5_out, xor_6_out, xor_7_out, xor_8_out, xor_9_out, xor_10_out,
       xor_11_out, xor_12_out, xor_13_out, xor_14_out, xor_15_out, xor_16_out, xor_17_out;

  xor xor_1 (xor_1_out, B7, SUB);
  xor xor_2 (xor_2_out, B0, SUB);
  xor xor_3 (xor_3_out, B1, SUB);
  xor xor_4 (xor_4_out, B2, SUB);
  xor xor_5 (xor_5_out, B3, SUB);
  xor xor_6 (xor_6_out, B4, SUB);
  xor xor_7 (xor_7_out, B5, SUB);
  xor xor_8 (xor_8_out, B6, SUB);
  xor xor_9 (xor_9_out, B7, SUB);
  not not_1 (not_1_out, xor_1_out);
  not not_2 (not_2_out, A7);
  not not_3 (not_3_out, Z7);
  xor xor_10 (xor_10_out, A0, xor_2_out);
  and and_1 (and_1_out, xor_2_out, A0);
  xor xor_11 (xor_11_out, A1, xor_3_out);
  and and_2 (and_2_out, xor_3_out, A1);
  xor xor_12 (xor_12_out, A2, xor_4_out);
  and and_3 (and_3_out, xor_4_out, A2);
  xor xor_13 (xor_13_out, A3, xor_5_out);
  and and_4 (and_4_out, xor_5_out, A3);
  xor xor_14 (xor_14_out, A4, xor_6_out);
  and and_5 (and_5_out, xor_6_out, A4);
  xor xor_15 (xor_15_out, A5, xor_7_out);
  and and_6 (and_6_out, xor_7_out, A5);
  xor xor_16 (xor_16_out, A6, xor_8_out);
  and and_7 (and_7_out, xor_8_out, A6);
  xor xor_17 (xor_17_out, A7, xor_9_out);
  and and_8 (and_8_out, not_1_out, not_2_out, Z7);
  and and_9 (and_9_out, not_3_out, xor_1_out, A7);
  and and_10 (and_10_out, SUB, xor_10_out);
  or or_1 (or_1_out, and_1_out, and_10_out);
  and and_11 (and_11_out, or_1_out, xor_11_out);
  or or_2 (or_2_out, and_2_out, and_11_out);
  and and_12 (and_12_out, or_2_out, xor_12_out);
  or or_3 (or_3_out, and_3_out, and_12_out);
  and and_13 (and_13_out, or_3_out, xor_13_out);
  or or_4 (or_4_out, and_4_out, and_13_out);
  and and_14 (and_14_out, or_4_out, xor_14_out);
  or or_5 (or_5_out, and_5_out, and_14_out);
  and and_15 (and_15_out, or_5_out, xor_15_out);
  or or_6 (or_6_out, and_6_out, and_15_out);
  and and_16 (and_16_out, or_6_out, xor_16_out);
  or or_7 (or_7_out, and_7_out, and_16_out);
  or or_8 (OVERFLOW, and_8_out, and_9_out);
  xor xor_18 (Z0, SUB, xor_10_out);
  xor xor_19 (Z1, or_1_out, xor_11_out);
  xor xor_20 (Z2, or_2_out, xor_12_out);
  xor xor_21 (Z3, or_3_out, xor_13_out);
  xor xor_22 (Z4, or_4_out, xor_14_out);
  xor xor_23 (Z5, or_5_out, xor_15_out);
  xor xor_24 (Z6, or_6_out, xor_16_out);
  xor xor_25 (Z7, or_7_out, xor_17_out);
endmodule

module LOGIC_Or (
  input  A0,
  input  B0,
  input  A1,
  input  B1,
  input  A2,
  input  B2,
  input  A3,
  input  B3,
  input  A4,
  input  B4,
  input  A5,
  input  B5,
  input  A6,
  input  B6,
  input  A7,
  input  B7,
  output Z0,
  output Z1,
  output Z2,
  output Z3,
  output Z4,
  output Z5,
  output Z6,
  output Z7
);

  or or_1 (Z0, A0, B0);
  or or_2 (Z1, A1, B1);
  or or_3 (Z2, A2, B2);
  or or_4 (Z3, A3, B3);
  or or_5 (Z4, A4, B4);
  or or_6 (Z5, A5, B5);
  or or_7 (Z6, A6, B6);
  or or_8 (Z7, A7, B7);
endmodule

module LOGIC_And (
  input  A0,
  input  B0,
  input  A1,
  input  B1,
  input  A2,
  input  B2,
  input  A3,
  input  B3,
  input  A4,
  input  B4,
  input  A5,
  input  B5,
  input  A6,
  input  B6,
  input  A7,
  input  B7,
  output Z0,
  output Z1,
  output Z2,
  output Z3,
  output Z4,
  output Z5,
  output Z6,
  output Z7
);

  and and_1 (Z0, A0, B0);
  and and_2 (Z1, A1, B1);
  and and_3 (Z2, A2, B2);
  and and_4 (Z3, A3, B3);
  and and_5 (Z4, A4, B4);
  and and_6 (Z5, A5, B5);
  and and_7 (Z6, A6, B6);
  and and_8 (Z7, A7, B7);
endmodule

module ALU_Register (
  input  CLOCK,
  input  D0,
  input  D1,
  input  D2,
  input  D3,
  input  D4,
  input  D5,
  input  D6,
  input  D7,
  output Z0,
  output Z1,
  output Z2,
  output Z3,
  output Z4,
  output Z5,
  output Z6,
  output Z7
);

  wire nand_1_out, nand_2_out, nand_3_out, nand_4_out, nand_5_out, nand_6_out, nand_7_out, nand_8_out,
       nand_9_out, nand_10_out, nand_11_out, nand_12_out, nand_13_out, nand_14_out, nand_15_out, nand_16_out,
       nand_25_out, nand_26_out, nand_27_out, nand_28_out, nand_29_out, nand_30_out, nand_31_out,
       nand_32_out, not_1_out, not_2_out, not_3_out, not_4_out, not_5_out, not_6_out, not_7_out, not_8_out;

  not not_1 (not_1_out, D0);
  not not_2 (not_2_out, D1);
  not not_3 (not_3_out, D2);
  not not_4 (not_4_out, D3);
  not not_5 (not_5_out, D4);
  not not_6 (not_6_out, D5);
  not not_7 (not_7_out, D6);
  not not_8 (not_8_out, D7);
  nand nand_1 (nand_1_out, D0, CLOCK);
  nand nand_2 (nand_2_out, not_1_out, CLOCK);
  nand nand_3 (nand_3_out, D1, CLOCK);
  nand nand_4 (nand_4_out, not_2_out, CLOCK);
  nand nand_5 (nand_5_out, D2, CLOCK);
  nand nand_6 (nand_6_out, not_3_out, CLOCK);
  nand nand_7 (nand_7_out, D3, CLOCK);
  nand nand_8 (nand_8_out, not_4_out, CLOCK);
  nand nand_9 (nand_9_out, D4, CLOCK);
  nand nand_10 (nand_10_out, not_5_out, CLOCK);
  nand nand_11 (nand_11_out, D5, CLOCK);
  nand nand_12 (nand_12_out, not_6_out, CLOCK);
  nand nand_13 (nand_13_out, D6, CLOCK);
  nand nand_14 (nand_14_out, not_7_out, CLOCK);
  nand nand_15 (nand_15_out, D7, CLOCK);
  nand nand_16 (nand_16_out, not_8_out, CLOCK);
  nand nand_17 (Z0, nand_1_out, nand_25_out);
  nand nand_18 (Z1, nand_3_out, nand_26_out);
  nand nand_19 (Z2, nand_5_out, nand_27_out);
  nand nand_20 (Z3, nand_7_out, nand_28_out);
  nand nand_21 (Z4, nand_9_out, nand_29_out);
  nand nand_22 (Z5, nand_11_out, nand_30_out);
  nand nand_23 (Z6, nand_13_out, nand_31_out);
  nand nand_24 (Z7, nand_15_out, nand_32_out);
  nand nand_25 (nand_25_out, Z0, nand_2_out);
  nand nand_26 (nand_26_out, Z1, nand_4_out);
  nand nand_27 (nand_27_out, Z2, nand_6_out);
  nand nand_28 (nand_28_out, Z3, nand_8_out);
  nand nand_29 (nand_29_out, Z4, nand_10_out);
  nand nand_30 (nand_30_out, Z5, nand_12_out);
  nand nand_31 (nand_31_out, Z6, nand_14_out);
  nand nand_32 (nand_32_out, Z7, nand_16_out);
endmodule

module LOGIC_Xor (
  input  A0,
  input  B0,
  input  A1,
  input  B1,
  input  A2,
  input  B2,
  input  A3,
  input  B3,
  input  A4,
  input  B4,
  input  A5,
  input  B5,
  input  A6,
  input  B6,
  input  A7,
  input  B7,
  output Z0,
  output Z1,
  output Z2,
  output Z3,
  output Z4,
  output Z5,
  output Z6,
  output Z7
);

  xor xor_1 (Z0, A0, B0);
  xor xor_2 (Z1, A1, B1);
  xor xor_3 (Z2, A2, B2);
  xor xor_4 (Z3, A3, B3);
  xor xor_5 (Z4, A4, B4);
  xor xor_6 (Z5, A5, B5);
  xor xor_7 (Z6, A6, B6);
  xor xor_8 (Z7, A7, B7);
endmodule

module ALU_Logic (
  input  A0,
  input  A1,
  input  A2,
  input  A3,
  input  A4,
  input  A5,
  input  A6,
  input  A7,
  input  B0,
  input  B1,
  input  B2,
  input  B3,
  input  B4,
  input  B5,
  input  B6,
  input  B7,
  input  S0,
  input  S1,
  output Z0,
  output Z1,
  output Z2,
  output Z3,
  output Z4,
  output Z5,
  output Z6,
  output Z7
);

  wire logic_and_1_z0, logic_and_1_z1, logic_and_1_z2, logic_and_1_z3, logic_and_1_z4, logic_and_1_z5,
       logic_and_1_z6, logic_and_1_z7, logic_or_1_z0, logic_or_1_z1, logic_or_1_z2, logic_or_1_z3,
       logic_or_1_z4, logic_or_1_z5, logic_or_1_z6, logic_or_1_z7, logic_xor_1_z0, logic_xor_1_z1,
       logic_xor_1_z2, logic_xor_1_z3, logic_xor_1_z4, logic_xor_1_z5, logic_xor_1_z6, logic_xor_1_z7,
       not_1_out, not_2_out, not_3_out, not_4_out, not_5_out, not_6_out, not_7_out, not_8_out;

  not not_1 (not_1_out, A0);
  not not_2 (not_2_out, A1);
  not not_3 (not_3_out, A2);
  not not_4 (not_4_out, A3);
  not not_5 (not_5_out, A4);
  not not_6 (not_6_out, A5);
  not not_7 (not_7_out, A6);
  not not_8 (not_8_out, A7);
  LOGIC_And logic_and_1 (
    .A0(A0), .B0(B0), .A1(A1), .B1(B1), .A2(A2), .B2(B2), .A3(A3), .B3(B3), .A4(A4), .B4(B4), .A5(A5),
    .B5(B5), .A6(A6), .B6(B6), .A7(A7), .B7(B7), .Z0(logic_and_1_z0), .Z1(logic_and_1_z1),
    .Z2(logic_and_1_z2), .Z3(logic_and_1_z3), .Z4(logic_and_1_z4), .Z5(logic_and_1_z5), .Z6(logic_and_1_z6),
    .Z7(logic_and_1_z7));
  LOGIC_Or logic_or_1 (
    .A0(A0), .B0(B0), .A1(A1), .B1(B1), .A2(A2), .B2(B2), .A3(A3), .B3(B3), .A4(A4), .B4(B4), .A5(A5),
    .B5(B5), .A6(A6), .B6(B6), .A7(A7), .B7(B7), .Z0(logic_or_1_z0), .Z1(logic_or_1_z1), .Z2(logic_or_1_z2),
    .Z3(logic_or_1_z3), .Z4(logic_or_1_z4), .Z5(logic_or_1_z5), .Z6(logic_or_1_z6), .Z7(logic_or_1_z7));
  LOGIC_Xor logic_xor_1 (
    .A0(A0), .B0(B0), .A1(A1), .B1(B1), .A2(A2), .B2(B2), .A3(A3), .B3(B3), .A4(A4), .B4(B4), .A5(A5),
    .B5(B5), .A6(A6), .B6(B6), .A7(A7), .B7(B7), .Z0(logic_xor_1_z0), .Z1(logic_xor_1_z1),
    .Z2(logic_xor_1_z2), .Z3(logic_xor_1_z3), .Z4(logic_xor_1_z4), .Z5(logic_xor_1_z5), .Z6(logic_xor_1_z6),
    .Z7(logic_xor_1_z7));
  ALU_MultiplexerX4 alu_multiplexerx4_1 (
    .S0(S0), .S1(S1), .D0(not_1_out), .D1(logic_and_1_z0), .D2(logic_or_1_z0), .D3(logic_xor_1_z0), .Z(Z0));
  ALU_MultiplexerX4 alu_multiplexerx4_2 (
    .S0(S0), .S1(S1), .D0(not_2_out), .D1(logic_and_1_z1), .D2(logic_or_1_z1), .D3(logic_xor_1_z1), .Z(Z1));
  ALU_MultiplexerX4 alu_multiplexerx4_3 (
    .S0(S0), .S1(S1), .D0(not_3_out), .D1(logic_and_1_z2), .D2(logic_or_1_z2), .D3(logic_xor_1_z2), .Z(Z2));
  ALU_MultiplexerX4 alu_multiplexerx4_4 (
    .S0(S0), .S1(S1), .D0(not_4_out), .D1(logic_and_1_z3), .D2(logic_or_1_z3), .D3(logic_xor_1_z3), .Z(Z3));
  ALU_MultiplexerX4 alu_multiplexerx4_5 (
    .S0(S0), .S1(S1), .D0(not_5_out), .D1(logic_and_1_z4), .D2(logic_or_1_z4), .D3(logic_xor_1_z4), .Z(Z4));
  ALU_MultiplexerX4 alu_multiplexerx4_6 (
    .S0(S0), .S1(S1), .D0(not_6_out), .D1(logic_and_1_z5), .D2(logic_or_1_z5), .D3(logic_xor_1_z5), .Z(Z5));
  ALU_MultiplexerX4 alu_multiplexerx4_7 (
    .S0(S0), .S1(S1), .D0(not_7_out), .D1(logic_and_1_z6), .D2(logic_or_1_z6), .D3(logic_xor_1_z6), .Z(Z6));
  ALU_MultiplexerX4 alu_multiplexerx4_8 (
    .S0(S0), .S1(S1), .D0(not_8_out), .D1(logic_and_1_z7), .D2(logic_or_1_z7), .D3(logic_xor_1_z7), .Z(Z7));
endmodule

module ALU_Arithmetic (
  input  A0,
  input  A1,
  input  A2,
  input  A3,
  input  A4,
  input  A5,
  input  A6,
  input  A7,
  input  B0,
  input  B1,
  input  B2,
  input  B3,
  input  B4,
  input  B5,
  input  B6,
  input  B7,
  input  SUB,
  input  S0,
  input  S1,
  output Z0,
  output Z1,
  output Z2,
  output Z3,
  output Z4,
  output Z5,
  output Z6,
  output Z7,
  output OVERFLOW
);

  wire arithmetic_addersubtractor_1_overflow, arithmetic_addersubtractor_1_z0,
       arithmetic_addersubtractor_1_z1, arithmetic_addersubtractor_1_z2, arithmetic_addersubtractor_1_z3,
       arithmetic_addersubtractor_1_z4, arithmetic_addersubtractor_1_z5, arithmetic_addersubtractor_1_z6,
       arithmetic_addersubtractor_1_z7, arithmetic_divider_1_z0, arithmetic_divider_1_z1,
       arithmetic_divider_1_z2, arithmetic_divider_1_z3, arithmetic_divider_1_z4, arithmetic_divider_1_z5,
       arithmetic_divider_1_z6, arithmetic_divider_1_z7, arithmetic_multiplier_1_overflow,
       arithmetic_multiplier_1_z0, arithmetic_multiplier_1_z1, arithmetic_multiplier_1_z2,
       arithmetic_multiplier_1_z3, arithmetic_multiplier_1_z4, arithmetic_multiplier_1_z5,
       arithmetic_multiplier_1_z6, arithmetic_multiplier_1_z7;

  ARITHMETIC_AdderSubtractor arithmetic_addersubtractor_1 (
    .SUB(SUB), .A0(A0), .A1(A1), .A2(A2), .A3(A3), .A4(A4), .A5(A5), .A6(A6), .A7(A7), .B0(B0), .B1(B1),
    .B2(B2), .B3(B3), .B4(B4), .B5(B5), .B6(B6), .B7(B7), .Z0(arithmetic_addersubtractor_1_z0),
    .Z1(arithmetic_addersubtractor_1_z1), .Z2(arithmetic_addersubtractor_1_z2),
    .Z3(arithmetic_addersubtractor_1_z3), .Z4(arithmetic_addersubtractor_1_z4),
    .Z5(arithmetic_addersubtractor_1_z5), .Z6(arithmetic_addersubtractor_1_z6),
    .Z7(arithmetic_addersubtractor_1_z7), .OVERFLOW(arithmetic_addersubtractor_1_overflow));
  ARITHMETIC_Multiplier arithmetic_multiplier_1 (
    .A0(A0), .A1(A1), .A2(A2), .A3(A3), .A4(A4), .A5(A5), .A6(A6), .A7(A7), .B0(B0), .B1(B1), .B2(B2),
    .B3(B3), .B4(B4), .B5(B5), .B6(B6), .B7(B7), .Z0(arithmetic_multiplier_1_z0),
    .Z1(arithmetic_multiplier_1_z1), .Z2(arithmetic_multiplier_1_z2), .Z3(arithmetic_multiplier_1_z3),
    .Z4(arithmetic_multiplier_1_z4), .Z5(arithmetic_multiplier_1_z5), .Z6(arithmetic_multiplier_1_z6),
    .Z7(arithmetic_multiplier_1_z7), .OVERFLOW(arithmetic_multiplier_1_overflow));
  ARITHMETIC_Divider arithmetic_divider_1 (
    .A7(A7), .A6(A6), .B3(B3), .A5(A5), .B2(B2), .A4(A4), .B1(B1), .A3(A3), .B0(B0), .A2(A2), .A1(A1),
    .A0(A0), .Z3(arithmetic_divider_1_z3), .Z2(arithmetic_divider_1_z2), .Z1(arithmetic_divider_1_z1),
    .Z0(arithmetic_divider_1_z0), .Z7(arithmetic_divider_1_z7), .Z6(arithmetic_divider_1_z6),
    .Z5(arithmetic_divider_1_z5), .Z4(arithmetic_divider_1_z4));
  ALU_MultiplexerX4 alu_multiplexerx4_1 (
    .S0(S0), .S1(S1), .D0(arithmetic_addersubtractor_1_z0), .D1(arithmetic_multiplier_1_z0),
    .D2(arithmetic_divider_1_z0), .Z(Z0));  // open: D3
  ALU_MultiplexerX4 alu_multiplexerx4_2 (
    .S0(S0), .S1(S1), .D0(arithmetic_addersubtractor_1_z1), .D1(arithmetic_multiplier_1_z1),
    .D2(arithmetic_divider_1_z1), .Z(Z1));  // open: D3
  ALU_MultiplexerX4 alu_multiplexerx4_3 (
    .S0(S0), .S1(S1), .D0(arithmetic_addersubtractor_1_z2), .D1(arithmetic_multiplier_1_z2),
    .D2(arithmetic_divider_1_z2), .Z(Z2));  // open: D3
  ALU_MultiplexerX4 alu_multiplexerx4_4 (
    .S0(S0), .S1(S1), .D0(arithmetic_addersubtractor_1_z3), .D1(arithmetic_multiplier_1_z3),
    .D2(arithmetic_divider_1_z3), .Z(Z3));  // open: D3
  ALU_MultiplexerX4 alu_multiplexerx4_5 (
    .S0(S0), .S1(S1), .D0(arithmetic_addersubtractor_1_z4), .D1(arithmetic_multiplier_1_z4),
    .D2(arithmetic_divider_1_z4), .Z(Z4));  // open: D3
  ALU_MultiplexerX4 alu_multiplexerx4_6 (
    .S0(S0), .S1(S1), .D0(arithmetic_addersubtractor_1_z5), .D1(arithmetic_multiplier_1_z5),
    .D2(arithmetic_divider_1_z5), .Z(Z5));  // open: D3
  ALU_MultiplexerX4 alu_multiplexerx4_7 (
    .S0(S0), .S1(S1), .D0(arithmetic_addersubtractor_1_z6), .D1(arithmetic_multiplier_1_z6),
    .D2(arithmetic_divider_1_z6), .Z(Z6));  // open: D3
  ALU_MultiplexerX4 alu_multiplexerx4_8 (
    .S0(S0), .S1(S1), .D0(arithmetic_addersubtractor_1_z7), .D1(arithmetic_multiplier_1_z7),
    .D2(arithmetic_divider_1_z7), .Z(Z7));  // open: D3
  ALU_MultiplexerX4 alu_multiplexerx4_9 (
    .S0(S0), .S1(S1), .D0(arithmetic_addersubtractor_1_overflow), .D1(arithmetic_multiplier_1_overflow),
    .Z(OVERFLOW));  // open: D2, D3
endmodule

module ALU_MultiplexerX2 (
  input  S3,
  input  D0,
  input  D1,
  output Z
);

  wire and_1_out, and_2_out, not_1_out;

  not not_1 (not_1_out, S3);
  and and_1 (and_1_out, not_1_out, D0);
  and and_2 (and_2_out, S3, D1);
  or or_1 (Z, and_1_out, and_2_out);
endmodule

module ARITHMETIC_Divider (
  input  A7,
  input  A6,
  input  B3,
  input  A5,
  input  B2,
  input  A4,
  input  B1,
  input  A3,
  input  B0,
  input  A2,
  input  A1,
  input  A0,
  output Z3,
  output Z2,
  output Z1,
  output Z0,
  output Z7,
  output Z6,
  output Z5,
  output Z4
);

  wire divider_fullsubtractor_1_bout, divider_fullsubtractor_1_z, divider_fullsubtractor_2_bout,
       divider_fullsubtractor_2_z, divider_fullsubtractor_3_bout, divider_fullsubtractor_3_z,
       divider_fullsubtractor_4_bout, divider_fullsubtractor_4_z, divider_fullsubtractor_5_bout,
       divider_fullsubtractor_5_z, divider_fullsubtractor_6_bout, divider_fullsubtractor_6_z,
       divider_fullsubtractor_7_bout, divider_fullsubtractor_7_z, divider_fullsubtractor_8_bout,
       divider_fullsubtractor_8_z, divider_fullsubtractor_9_bout, divider_fullsubtractor_9_z,
       divider_fullsubtractor_10_bout, divider_fullsubtractor_11_bout, divider_fullsubtractor_11_z,
       divider_fullsubtractor_12_bout, divider_fullsubtractor_12_z, divider_fullsubtractor_13_bout,
       divider_fullsubtractor_14_bout, divider_fullsubtractor_14_z, divider_fullsubtractor_15_bout,
       divider_fullsubtractor_16_bout, not_1_out, not_2_out, not_3_out, not_4_out;

  or or_1 (Z3, not_1_out, A7);
  not not_1 (not_1_out, divider_fullsubtractor_1_bout);
  DIVIDER_FullSubtractor divider_fullsubtractor_1 (
    .A(A6), .B(B3), .S(Z3), .Bin(divider_fullsubtractor_2_bout), .Z(divider_fullsubtractor_1_z),
    .Bout(divider_fullsubtractor_1_bout));
  or or_2 (Z2, not_2_out, divider_fullsubtractor_1_z);
  DIVIDER_FullSubtractor divider_fullsubtractor_2 (
    .A(A5), .B(B2), .S(Z3), .Bin(divider_fullsubtractor_4_bout), .Z(divider_fullsubtractor_2_z),
    .Bout(divider_fullsubtractor_2_bout));
  not not_2 (not_2_out, divider_fullsubtractor_3_bout);
  DIVIDER_FullSubtractor divider_fullsubtractor_3 (
    .A(divider_fullsubtractor_2_z), .B(B3), .S(Z2), .Bin(divider_fullsubtractor_5_bout),
    .Z(divider_fullsubtractor_3_z), .Bout(divider_fullsubtractor_3_bout));
  or or_3 (Z1, not_3_out, divider_fullsubtractor_3_z);
  DIVIDER_FullSubtractor divider_fullsubtractor_4 (
    .A(A4), .B(B1), .S(Z3), .Bin(divider_fullsubtractor_7_bout), .Z(divider_fullsubtractor_4_z),
    .Bout(divider_fullsubtractor_4_bout));
  DIVIDER_FullSubtractor divider_fullsubtractor_5 (
    .A(divider_fullsubtractor_4_z), .B(B2), .S(Z2), .Bin(divider_fullsubtractor_8_bout),
    .Z(divider_fullsubtractor_5_z), .Bout(divider_fullsubtractor_5_bout));
  not not_3 (not_3_out, divider_fullsubtractor_6_bout);
  DIVIDER_FullSubtractor divider_fullsubtractor_6 (
    .A(divider_fullsubtractor_5_z), .B(B3), .S(Z1), .Bin(divider_fullsubtractor_9_bout),
    .Z(divider_fullsubtractor_6_z), .Bout(divider_fullsubtractor_6_bout));
  or or_4 (Z0, not_4_out, divider_fullsubtractor_6_z);
  DIVIDER_FullSubtractor divider_fullsubtractor_7 (
    .A(A3), .B(B0), .S(Z3), .Z(divider_fullsubtractor_7_z), .Bout(divider_fullsubtractor_7_bout));  // open: Bin
  DIVIDER_FullSubtractor divider_fullsubtractor_8 (
    .A(divider_fullsubtractor_7_z), .B(B1), .S(Z2), .Bin(divider_fullsubtractor_11_bout),
    .Z(divider_fullsubtractor_8_z), .Bout(divider_fullsubtractor_8_bout));
  DIVIDER_FullSubtractor divider_fullsubtractor_9 (
    .A(divider_fullsubtractor_8_z), .B(B2), .S(Z1), .Bin(divider_fullsubtractor_12_bout),
    .Z(divider_fullsubtractor_9_z), .Bout(divider_fullsubtractor_9_bout));
  not not_4 (not_4_out, divider_fullsubtractor_10_bout);
  DIVIDER_FullSubtractor divider_fullsubtractor_10 (
    .A(divider_fullsubtractor_9_z), .B(B3), .S(Z0), .Bin(divider_fullsubtractor_13_bout), .Z(Z7),
    .Bout(divider_fullsubtractor_10_bout));
  DIVIDER_FullSubtractor divider_fullsubtractor_11 (
    .A(A2), .B(B0), .S(Z2), .Z(divider_fullsubtractor_11_z), .Bout(divider_fullsubtractor_11_bout));  // open: Bin
  DIVIDER_FullSubtractor divider_fullsubtractor_12 (
    .A(divider_fullsubtractor_11_z), .B(B1), .S(Z1), .Bin(divider_fullsubtractor_14_bout),
    .Z(divider_fullsubtractor_12_z), .Bout(divider_fullsubtractor_12_bout));
  DIVIDER_FullSubtractor divider_fullsubtractor_13 (
    .A(divider_fullsubtractor_12_z), .B(B2), .S(Z0), .Bin(divider_fullsubtractor_15_bout), .Z(Z6),
    .Bout(divider_fullsubtractor_13_bout));
  DIVIDER_FullSubtractor divider_fullsubtractor_14 (
    .A(A1), .B(B0), .S(Z1), .Z(divider_fullsubtractor_14_z), .Bout(divider_fullsubtractor_14_bout));  // open: Bin
  DIVIDER_FullSubtractor divider_fullsubtractor_15 (
    .A(divider_fullsubtractor_14_z), .B(B1), .S(Z0), .Bin(divider_fullsubtractor_16_bout), .Z(Z5),
    .Bout(divider_fullsubtractor_15_bout));
  DIVIDER_FullSubtractor divider_fullsubtractor_16 (
    .A(A0), .B(B0), .S(Z0), .Z(Z4), .Bout(divider_fullsubtractor_16_bout));  // open: Bin
endmodule

module ARITHMETIC_Multiplier (
  input  A0,
  input  A1,
  input  A2,
  input  A3,
  input  A4,
  input  A5,
  input  A6,
  input  A7,
  input  B0,
  input  B1,
  input  B2,
  input  B3,
  input  B4,
  input  B5,
  input  B6,
  input  B7,
  output Z0,
  output Z1,
  output Z2,
  output Z3,
  output Z4,
  output Z5,
  output Z6,
  output Z7,
  output OVERFLOW
);

  wire and_2_out, and_3_out, and_4_out, and_5_out, and_6_out, and_7_out, multiplier_partialadder_1_cout,
       multiplier_partialadder_1_xout, multiplier_partialadder_1_yout, multiplier_partialadder_2_cout,
       multiplier_partialadder_2_xout, multiplier_partialadder_2_xyout, multiplier_partialadder_2_yout,
       multiplier_partialadder_3_cout, multiplier_partialadder_3_xout, multiplier_partialadder_3_xyout,
       multiplier_partialadder_3_yout, multiplier_partialadder_4_cout, multiplier_partialadder_4_xout,
       multiplier_partialadder_4_xyout, multiplier_partialadder_4_yout, multiplier_partialadder_5_cout,
       multiplier_partialadder_5_xout, multiplier_partialadder_5_xyout, multiplier_partialadder_5_yout,
       multiplier_partialadder_6_cout, multiplier_partialadder_6_xout, multiplier_partialadder_6_xyout,
       multiplier_partialadder_6_yout, multiplier_partialadder_7_cout, multiplier_partialadder_7_xout,
       multiplier_partialadder_7_xyout, multiplier_partialadder_7_yout, multiplier_partialadder_8_cout,
       multiplier_partialadder_8_xout, multiplier_partialadder_8_yout, multiplier_partialadder_9_cout,
       multiplier_partialadder_9_xout, multiplier_partialadder_9_xyout, multiplier_partialadder_9_yout,
       multiplier_partialadder_10_cout, multiplier_partialadder_10_xout, multiplier_partialadder_10_xyout,
       multiplier_partialadder_10_yout, multiplier_partialadder_11_cout, multiplier_partialadder_11_xout,
       multiplier_partialadder_11_xyout, multiplier_partialadder_11_yout, multiplier_partialadder_12_cout,
       multiplier_partialadder_12_xout, multiplier_partialadder_12_xyout, multiplier_partialadder_12_yout,
       multiplier_partialadder_13_cout, multiplier_partialadder_13_xout, multiplier_partialadder_13_xyout,
       multiplier_partialadder_13_yout, multiplier_partialadder_14_cout, multiplier_partialadder_14_xout,
       multiplier_partialadder_14_xyout, multiplier_partialadder_14_yout, multiplier_partialadder_15_cout,
       multiplier_partialadder_15_xout, multiplier_partialadder_15_yout, multiplier_partialadder_16_cout,
       multiplier_partialadder_16_xout, multiplier_partialadder_16_xyout, multiplier_partialadder_16_yout,
       multiplier_partialadder_17_cout, multiplier_partialadder_17_xout, multiplier_partialadder_17_xyout,
       multiplier_partialadder_17_yout, multiplier_partialadder_18_cout, multiplier_partialadder_18_xout,
       multiplier_partialadder_18_xyout, multiplier_partialadder_18_yout, multiplier_partialadder_19_cout,
       multiplier_partialadder_19_xout, multiplier_partialadder_19_xyout, multiplier_partialadder_19_yout,
       multiplier_partialadder_20_cout, multiplier_partialadder_20_xout, multiplier_partialadder_20_xyout,
       multiplier_partialadder_20_yout, multiplier_partialadder_21_cout, multiplier_partialadder_21_xout,
       multiplier_partialadder_21_xyout, multiplier_partialadder_21_yout, multiplier_partialadder_22_cout,
       multiplier_partialadder_22_xout, multiplier_partialadder_22_yout, multiplier_partialadder_23_cout,
       multiplier_partialadder_23_xout, multiplier_partialadder_23_xyout, multiplier_partialadder_23_yout,
       multiplier_partialadder_24_cout, multiplier_partialadder_24_xout, multiplier_partialadder_24_xyout,
       multiplier_partialadder_24_yout, multiplier_partialadder_25_cout, multiplier_partialadder_25_xout,
       multiplier_partialadder_25_xyout, multiplier_partialadder_25_yout, multiplier_partialadder_26_cout,
       multiplier_partialadder_26_xout, multiplier_partialadder_26_xyout, multiplier_partialadder_26_yout,
       multiplier_partialadder_27_cout, multiplier_partialadder_27_xout, multiplier_partialadder_27_xyout,
       multiplier_partialadder_27_yout, multiplier_partialadder_28_cout, multiplier_partialadder_28_xout,
       multiplier_partialadder_28_xyout, multiplier_partialadder_28_yout, multiplier_partialadder_29_cout,
       multiplier_partialadder_29_xout, multiplier_partialadder_29_yout, multiplier_partialadder_30_cout,
       multiplier_partialadder_30_xout, multiplier_partialadder_30_xyout, multiplier_partialadder_30_yout,
       multiplier_partialadder_31_cout, multiplier_partialadder_31_xout, multiplier_partialadder_31_xyout,
       multiplier_partialadder_31_yout, multiplier_partialadder_32_cout, multiplier_partialadder_32_xout,
       multiplier_partialadder_32_xyout, multiplier_partialadder_32_yout, multiplier_partialadder_33_cout,
       multiplier_partialadder_33_xout, multiplier_partialadder_33_xyout, multiplier_partialadder_33_yout,
       multiplier_partialadder_34_cout, multiplier_partialadder_34_xout, multiplier_partialadder_34_xyout,
       multiplier_partialadder_34_yout, multiplier_partialadder_35_cout, multiplier_partialadder_35_xout,
       multiplier_partialadder_35_xyout, multiplier_partialadder_35_yout, multiplier_partialadder_36_cout,
       multiplier_partialadder_36_xout, multiplier_partialadder_36_yout, multiplier_partialadder_37_cout,
       multiplier_partialadder_37_xout, multiplier_partialadder_37_xyout, multiplier_partialadder_37_yout,
       multiplier_partialadder_38_cout, multiplier_partialadder_38_xout, multiplier_partialadder_38_xyout,
       multiplier_partialadder_38_yout, multiplier_partialadder_39_cout, multiplier_partialadder_39_xout,
       multiplier_partialadder_39_xyout, multiplier_partialadder_39_yout, multiplier_partialadder_40_cout,
       multiplier_partialadder_40_xout, multiplier_partialadder_40_xyout, multiplier_partialadder_40_yout,
       multiplier_partialadder_41_cout, multiplier_partialadder_41_xout, multiplier_partialadder_41_xyout,
       multiplier_partialadder_41_yout, multiplier_partialadder_42_cout, multiplier_partialadder_42_xout,
       multiplier_partialadder_42_xyout, multiplier_partialadder_42_yout, multiplier_partialadder_43_cout,
       multiplier_partialadder_43_xyout, multiplier_partialadder_44_xyout, multiplier_partialaddernot_1_cout,
       multiplier_partialaddernot_1_xout, multiplier_partialaddernot_1_xyout,
       multiplier_partialaddernot_2_cout, multiplier_partialaddernot_2_xout,
       multiplier_partialaddernot_2_xyout, multiplier_partialaddernot_3_cout,
       multiplier_partialaddernot_3_xout, multiplier_partialaddernot_3_xyout,
       multiplier_partialaddernot_4_cout, multiplier_partialaddernot_4_xout,
       multiplier_partialaddernot_4_xyout, multiplier_partialaddernot_5_cout,
       multiplier_partialaddernot_5_xout, multiplier_partialaddernot_5_xyout,
       multiplier_partialaddernot_6_cout, multiplier_partialaddernot_6_xout,
       multiplier_partialaddernot_6_xyout, multiplier_partialaddernot_7_cout,
       multiplier_partialaddernot_7_yout, multiplier_partialaddernot_8_cout,
       multiplier_partialaddernot_8_xyout, multiplier_partialaddernot_8_yout,
       multiplier_partialaddernot_9_cout, multiplier_partialaddernot_9_xyout,
       multiplier_partialaddernot_9_yout, multiplier_partialaddernot_10_cout,
       multiplier_partialaddernot_10_xyout, multiplier_partialaddernot_10_yout,
       multiplier_partialaddernot_11_cout, multiplier_partialaddernot_11_xyout,
       multiplier_partialaddernot_11_yout, multiplier_partialaddernot_12_cout,
       multiplier_partialaddernot_12_xyout, multiplier_partialaddernot_12_yout,
       multiplier_partialaddernot_13_cout, multiplier_partialaddernot_13_xyout,
       multiplier_partialaddernot_13_yout, nand_1_out, xor_1_out, xor_2_out, xor_3_out, xor_4_out, xor_5_out,
       xor_6_out, xor_7_out, xor_8_out;

  and and_1 (Z0, A0, B0);
  and and_2 (and_2_out, A0, B1);
  and and_3 (and_3_out, A0, B2);
  and and_4 (and_4_out, A0, B3);
  and and_5 (and_5_out, A0, B4);
  and and_6 (and_6_out, A0, B5);
  and and_7 (and_7_out, A0, B6);
  nand nand_1 (nand_1_out, A0, B7);
  MULTIPLIER_PartialAdder multiplier_partialadder_1 (
    .Z(and_2_out), .Xin(B0), .Yin(A1), .Cin(1'b0), .Yout(multiplier_partialadder_1_yout),
    .Cout(multiplier_partialadder_1_cout), .XYout(Z1), .Xout(multiplier_partialadder_1_xout));
  MULTIPLIER_PartialAdder multiplier_partialadder_2 (
    .Z(and_3_out), .Xin(B1), .Yin(multiplier_partialadder_1_yout), .Cin(multiplier_partialadder_1_cout),
    .Yout(multiplier_partialadder_2_yout), .Cout(multiplier_partialadder_2_cout),
    .XYout(multiplier_partialadder_2_xyout), .Xout(multiplier_partialadder_2_xout));
  MULTIPLIER_PartialAdder multiplier_partialadder_3 (
    .Z(and_4_out), .Xin(B2), .Yin(multiplier_partialadder_2_yout), .Cin(multiplier_partialadder_2_cout),
    .Yout(multiplier_partialadder_3_yout), .Cout(multiplier_partialadder_3_cout),
    .XYout(multiplier_partialadder_3_xyout), .Xout(multiplier_partialadder_3_xout));
  MULTIPLIER_PartialAdder multiplier_partialadder_4 (
    .Z(and_5_out), .Xin(B3), .Yin(multiplier_partialadder_3_yout), .Cin(multiplier_partialadder_3_cout),
    .Yout(multiplier_partialadder_4_yout), .Cout(multiplier_partialadder_4_cout),
    .XYout(multiplier_partialadder_4_xyout), .Xout(multiplier_partialadder_4_xout));
  MULTIPLIER_PartialAdder multiplier_partialadder_5 (
    .Z(and_6_out), .Xin(B4), .Yin(multiplier_partialadder_4_yout), .Cin(multiplier_partialadder_4_cout),
    .Yout(multiplier_partialadder_5_yout), .Cout(multiplier_partialadder_5_cout),
    .XYout(multiplier_partialadder_5_xyout), .Xout(multiplier_partialadder_5_xout));
  MULTIPLIER_PartialAdder multiplier_partialadder_6 (
    .Z(and_7_out), .Xin(B5), .Yin(multiplier_partialadder_5_yout), .Cin(multiplier_partialadder_5_cout),
    .Yout(multiplier_partialadder_6_yout), .Cout(multiplier_partialadder_6_cout),
    .XYout(multiplier_partialadder_6_xyout), .Xout(multiplier_partialadder_6_xout));
  MULTIPLIER_PartialAdder multiplier_partialadder_7 (
    .Z(nand_1_out), .Xin(B6), .Yin(multiplier_partialadder_6_yout), .Cin(multiplier_partialadder_6_cout),
    .Yout(multiplier_partialadder_7_yout), .Cout(multiplier_partialadder_7_cout),
    .XYout(multiplier_partialadder_7_xyout), .Xout(multiplier_partialadder_7_xout));
  MULTIPLIER_PartialAdderNot multiplier_partialaddernot_1 (
    .Z(1'b1), .Xin(B7), .Yin(multiplier_partialadder_7_yout), .Cin(multiplier_partialadder_7_cout),
    .Cout(multiplier_partialaddernot_1_cout), .XYout(multiplier_partialaddernot_1_xyout),
    .Xout(multiplier_partialaddernot_1_xout));  // open: Yout
  MULTIPLIER_PartialAdder multiplier_partialadder_8 (
    .Z(multiplier_partialadder_2_xyout), .Xin(multiplier_partialadder_1_xout), .Yin(A2), .Cin(1'b0),
    .Yout(multiplier_partialadder_8_yout), .Cout(multiplier_partialadder_8_cout), .XYout(Z2),
    .Xout(multiplier_partialadder_8_xout));
  MULTIPLIER_PartialAdder multiplier_partialadder_9 (
    .Z(multiplier_partialadder_3_xyout), .Xin(multiplier_partialadder_2_xout),
    .Yin(multiplier_partialadder_8_yout), .Cin(multiplier_partialadder_8_cout),
    .Yout(multiplier_partialadder_9_yout), .Cout(multiplier_partialadder_9_cout),
    .XYout(multiplier_partialadder_9_xyout), .Xout(multiplier_partialadder_9_xout));
  MULTIPLIER_PartialAdder multiplier_partialadder_10 (
    .Z(multiplier_partialadder_4_xyout), .Xin(multiplier_partialadder_3_xout),
    .Yin(multiplier_partialadder_9_yout), .Cin(multiplier_partialadder_9_cout),
    .Yout(multiplier_partialadder_10_yout), .Cout(multiplier_partialadder_10_cout),
    .XYout(multiplier_partialadder_10_xyout), .Xout(multiplier_partialadder_10_xout));
  MULTIPLIER_PartialAdder multiplier_partialadder_11 (
    .Z(multiplier_partialadder_5_xyout), .Xin(multiplier_partialadder_4_xout),
    .Yin(multiplier_partialadder_10_yout), .Cin(multiplier_partialadder_10_cout),
    .Yout(multiplier_partialadder_11_yout), .Cout(multiplier_partialadder_11_cout),
    .XYout(multiplier_partialadder_11_xyout), .Xout(multiplier_partialadder_11_xout));
  MULTIPLIER_PartialAdder multiplier_partialadder_12 (
    .Z(multiplier_partialadder_6_xyout), .Xin(multiplier_partialadder_5_xout),
    .Yin(multiplier_partialadder_11_yout), .Cin(multiplier_partialadder_11_cout),
    .Yout(multiplier_partialadder_12_yout), .Cout(multiplier_partialadder_12_cout),
    .XYout(multiplier_partialadder_12_xyout), .Xout(multiplier_partialadder_12_xout));
  MULTIPLIER_PartialAdder multiplier_partialadder_13 (
    .Z(multiplier_partialadder_7_xyout), .Xin(multiplier_partialadder_6_xout),
    .Yin(multiplier_partialadder_12_yout), .Cin(multiplier_partialadder_12_cout),
    .Yout(multiplier_partialadder_13_yout), .Cout(multiplier_partialadder_13_cout),
    .XYout(multiplier_partialadder_13_xyout), .Xout(multiplier_partialadder_13_xout));
  MULTIPLIER_PartialAdder multiplier_partialadder_14 (
    .Z(multiplier_partialaddernot_1_xyout), .Xin(multiplier_partialadder_7_xout),
    .Yin(multiplier_partialadder_13_yout), .Cin(multiplier_partialadder_13_cout),
    .Yout(multiplier_partialadder_14_yout), .Cout(multiplier_partialadder_14_cout),
    .XYout(multiplier_partialadder_14_xyout), .Xout(multiplier_partialadder_14_xout));
  MULTIPLIER_PartialAdderNot multiplier_partialaddernot_2 (
    .Z(multiplier_partialaddernot_1_cout), .Xin(multiplier_partialaddernot_1_xout),
    .Yin(multiplier_partialadder_14_yout), .Cin(multiplier_partialadder_14_cout),
    .Cout(multiplier_partialaddernot_2_cout), .XYout(multiplier_partialaddernot_2_xyout),
    .Xout(multiplier_partialaddernot_2_xout));  // open: Yout
  MULTIPLIER_PartialAdder multiplier_partialadder_15 (
    .Z(multiplier_partialadder_9_xyout), .Xin(multiplier_partialadder_8_xout), .Yin(A3), .Cin(1'b0),
    .Yout(multiplier_partialadder_15_yout), .Cout(multiplier_partialadder_15_cout), .XYout(Z3),
    .Xout(multiplier_partialadder_15_xout));
  MULTIPLIER_PartialAdder multiplier_partialadder_16 (
    .Z(multiplier_partialadder_10_xyout), .Xin(multiplier_partialadder_9_xout),
    .Yin(multiplier_partialadder_15_yout), .Cin(multiplier_partialadder_15_cout),
    .Yout(multiplier_partialadder_16_yout), .Cout(multiplier_partialadder_16_cout),
    .XYout(multiplier_partialadder_16_xyout), .Xout(multiplier_partialadder_16_xout));
  MULTIPLIER_PartialAdder multiplier_partialadder_17 (
    .Z(multiplier_partialadder_11_xyout), .Xin(multiplier_partialadder_10_xout),
    .Yin(multiplier_partialadder_16_yout), .Cin(multiplier_partialadder_16_cout),
    .Yout(multiplier_partialadder_17_yout), .Cout(multiplier_partialadder_17_cout),
    .XYout(multiplier_partialadder_17_xyout), .Xout(multiplier_partialadder_17_xout));
  MULTIPLIER_PartialAdder multiplier_partialadder_18 (
    .Z(multiplier_partialadder_12_xyout), .Xin(multiplier_partialadder_11_xout),
    .Yin(multiplier_partialadder_17_yout), .Cin(multiplier_partialadder_17_cout),
    .Yout(multiplier_partialadder_18_yout), .Cout(multiplier_partialadder_18_cout),
    .XYout(multiplier_partialadder_18_xyout), .Xout(multiplier_partialadder_18_xout));
  MULTIPLIER_PartialAdder multiplier_partialadder_19 (
    .Z(multiplier_partialadder_13_xyout), .Xin(multiplier_partialadder_12_xout),
    .Yin(multiplier_partialadder_18_yout), .Cin(multiplier_partialadder_18_cout),
    .Yout(multiplier_partialadder_19_yout), .Cout(multiplier_partialadder_19_cout),
    .XYout(multiplier_partialadder_19_xyout), .Xout(multiplier_partialadder_19_xout));
  MULTIPLIER_PartialAdder multiplier_partialadder_20 (
    .Z(multiplier_partialadder_14_xyout), .Xin(multiplier_partialadder_13_xout),
    .Yin(multiplier_partialadder_19_yout), .Cin(multiplier_partialadder_19_cout),
    .Yout(multiplier_partialadder_20_yout), .Cout(multiplier_partialadder_20_cout),
    .XYout(multiplier_partialadder_20_xyout), .Xout(multiplier_partialadder_20_xout));
  MULTIPLIER_PartialAdder multiplier_partialadder_21 (
    .Z(multiplier_partialaddernot_2_xyout), .Xin(multiplier_partialadder_14_xout),
    .Yin(multiplier_partialadder_20_yout), .Cin(multiplier_partialadder_20_cout),
    .Yout(multiplier_partialadder_21_yout), .Cout(multiplier_partialadder_21_cout),
    .XYout(multiplier_partialadder_21_xyout), .Xout(multiplier_partialadder_21_xout));
  MULTIPLIER_PartialAdderNot multiplier_partialaddernot_3 (
    .Z(multiplier_partialaddernot_2_cout), .Xin(multiplier_partialaddernot_2_xout),
    .Yin(multiplier_partialadder_21_yout), .Cin(multiplier_partialadder_21_cout),
    .Cout(multiplier_partialaddernot_3_cout), .XYout(multiplier_partialaddernot_3_xyout),
    .Xout(multiplier_partialaddernot_3_xout));  // open: Yout
  MULTIPLIER_PartialAdder multiplier_partialadder_22 (
    .Z(multiplier_partialadder_16_xyout), .Xin(multiplier_partialadder_15_xout), .Yin(A4), .Cin(1'b0),
    .Yout(multiplier_partialadder_22_yout), .Cout(multiplier_partialadder_22_cout), .XYout(Z4),
    .Xout(multiplier_partialadder_22_xout));
  MULTIPLIER_PartialAdder multiplier_partialadder_23 (
    .Z(multiplier_partialadder_17_xyout), .Xin(multiplier_partialadder_16_xout),
    .Yin(multiplier_partialadder_22_yout), .Cin(multiplier_partialadder_22_cout),
    .Yout(multiplier_partialadder_23_yout), .Cout(multiplier_partialadder_23_cout),
    .XYout(multiplier_partialadder_23_xyout), .Xout(multiplier_partialadder_23_xout));
  MULTIPLIER_PartialAdder multiplier_partialadder_24 (
    .Z(multiplier_partialadder_18_xyout), .Xin(multiplier_partialadder_17_xout),
    .Yin(multiplier_partialadder_23_yout), .Cin(multiplier_partialadder_23_cout),
    .Yout(multiplier_partialadder_24_yout), .Cout(multiplier_partialadder_24_cout),
    .XYout(multiplier_partialadder_24_xyout), .Xout(multiplier_partialadder_24_xout));
  MULTIPLIER_PartialAdder multiplier_partialadder_25 (
    .Z(multiplier_partialadder_19_xyout), .Xin(multiplier_partialadder_18_xout),
    .Yin(multiplier_partialadder_24_yout), .Cin(multiplier_partialadder_24_cout),
    .Yout(multiplier_partialadder_25_yout), .Cout(multiplier_partialadder_25_cout),
    .XYout(multiplier_partialadder_25_xyout), .Xout(multiplier_partialadder_25_xout));
  MULTIPLIER_PartialAdder multiplier_partialadder_26 (
    .Z(multiplier_partialadder_20_xyout), .Xin(multiplier_partialadder_19_xout),
    .Yin(multiplier_partialadder_25_yout), .Cin(multiplier_partialadder_25_cout),
    .Yout(multiplier_partialadder_26_yout), .Cout(multiplier_partialadder_26_cout),
    .XYout(multiplier_partialadder_26_xyout), .Xout(multiplier_partialadder_26_xout));
  MULTIPLIER_PartialAdder multiplier_partialadder_27 (
    .Z(multiplier_partialadder_21_xyout), .Xin(multiplier_partialadder_20_xout),
    .Yin(multiplier_partialadder_26_yout), .Cin(multiplier_partialadder_26_cout),
    .Yout(multiplier_partialadder_27_yout), .Cout(multiplier_partialadder_27_cout),
    .XYout(multiplier_partialadder_27_xyout), .Xout(multiplier_partialadder_27_xout));
  MULTIPLIER_PartialAdder multiplier_partialadder_28 (
    .Z(multiplier_partialaddernot_3_xyout), .Xin(multiplier_partialadder_21_xout),
    .Yin(multiplier_partialadder_27_yout), .Cin(multiplier_partialadder_27_cout),
    .Yout(multiplier_partialadder_28_yout), .Cout(multiplier_partialadder_28_cout),
    .XYout(multiplier_partialadder_28_xyout), .Xout(multiplier_partialadder_28_xout));
  MULTIPLIER_PartialAdderNot multiplier_partialaddernot_4 (
    .Z(multiplier_partialaddernot_3_cout), .Xin(multiplier_partialaddernot_3_xout),
    .Yin(multiplier_partialadder_28_yout), .Cin(multiplier_partialadder_28_cout),
    .Cout(multiplier_partialaddernot_4_cout), .XYout(multiplier_partialaddernot_4_xyout),
    .Xout(multiplier_partialaddernot_4_xout));  // open: Yout
  MULTIPLIER_PartialAdder multiplier_partialadder_29 (
    .Z(multiplier_partialadder_23_xyout), .Xin(multiplier_partialadder_22_xout), .Yin(A5), .Cin(1'b0),
    .Yout(multiplier_partialadder_29_yout), .Cout(multiplier_partialadder_29_cout), .XYout(Z5),
    .Xout(multiplier_partialadder_29_xout));
  MULTIPLIER_PartialAdder multiplier_partialadder_30 (
    .Z(multiplier_partialadder_24_xyout), .Xin(multiplier_partialadder_23_xout),
    .Yin(multiplier_partialadder_29_yout), .Cin(multiplier_partialadder_29_cout),
    .Yout(multiplier_partialadder_30_yout), .Cout(multiplier_partialadder_30_cout),
    .XYout(multiplier_partialadder_30_xyout), .Xout(multiplier_partialadder_30_xout));
  MULTIPLIER_PartialAdder multiplier_partialadder_31 (
    .Z(multiplier_partialadder_25_xyout), .Xin(multiplier_partialadder_24_xout),
    .Yin(multiplier_partialadder_30_yout), .Cin(multiplier_partialadder_30_cout),
    .Yout(multiplier_partialadder_31_yout), .Cout(multiplier_partialadder_31_cout),
    .XYout(multiplier_partialadder_31_xyout), .Xout(multiplier_partialadder_31_xout));
  MULTIPLIER_PartialAdder multiplier_partialadder_32 (
    .Z(multiplier_partialadder_26_xyout), .Xin(multiplier_partialadder_25_xout),
    .Yin(multiplier_partialadder_31_yout), .Cin(multiplier_partialadder_31_cout),
    .Yout(multiplier_partialadder_32_yout), .Cout(multiplier_partialadder_32_cout),
    .XYout(multiplier_partialadder_32_xyout), .Xout(multiplier_partialadder_32_xout));
  MULTIPLIER_PartialAdder multiplier_partialadder_33 (
    .Z(multiplier_partialadder_27_xyout), .Xin(multiplier_partialadder_26_xout),
    .Yin(multiplier_partialadder_32_yout), .Cin(multiplier_partialadder_32_cout),
    .Yout(multiplier_partialadder_33_yout), .Cout(multiplier_partialadder_33_cout),
    .XYout(multiplier_partialadder_33_xyout), .Xout(multiplier_partialadder_33_xout));
  MULTIPLIER_PartialAdder multiplier_partialadder_34 (
    .Z(multiplier_partialadder_28_xyout), .Xin(multiplier_partialadder_27_xout),
    .Yin(multiplier_partialadder_33_yout), .Cin(multiplier_partialadder_33_cout),
    .Yout(multiplier_partialadder_34_yout), .Cout(multiplier_partialadder_34_cout),
    .XYout(multiplier_partialadder_34_xyout), .Xout(multiplier_partialadder_34_xout));
  MULTIPLIER_PartialAdder multiplier_partialadder_35 (
    .Z(multiplier_partialaddernot_4_xyout), .Xin(multiplier_partialadder_28_xout),
    .Yin(multiplier_partialadder_34_yout), .Cin(multiplier_partialadder_34_cout),
    .Yout(multiplier_partialadder_35_yout), .Cout(multiplier_partialadder_35_cout),
    .XYout(multiplier_partialadder_35_xyout), .Xout(multiplier_partialadder_35_xout));
  MULTIPLIER_PartialAdderNot multiplier_partialaddernot_5 (
    .Z(multiplier_partialaddernot_4_cout), .Xin(multiplier_partialaddernot_4_xout),
    .Yin(multiplier_partialadder_35_yout), .Cin(multiplier_partialadder_35_cout),
    .Cout(multiplier_partialaddernot_5_cout), .XYout(multiplier_partialaddernot_5_xyout),
    .Xout(multiplier_partialaddernot_5_xout));  // open: Yout
  MULTIPLIER_PartialAdder multiplier_partialadder_36 (
    .Z(multiplier_partialadder_30_xyout), .Xin(multiplier_partialadder_29_xout), .Yin(A6), .Cin(1'b0),
    .Yout(multiplier_partialadder_36_yout), .Cout(multiplier_partialadder_36_cout), .XYout(Z6),
    .Xout(multiplier_partialadder_36_xout));
  MULTIPLIER_PartialAdder multiplier_partialadder_37 (
    .Z(multiplier_partialadder_31_xyout), .Xin(multiplier_partialadder_30_xout),
    .Yin(multiplier_partialadder_36_yout), .Cin(multiplier_partialadder_36_cout),
    .Yout(multiplier_partialadder_37_yout), .Cout(multiplier_partialadder_37_cout),
    .XYout(multiplier_partialadder_37_xyout), .Xout(multiplier_partialadder_37_xout));
  MULTIPLIER_PartialAdder multiplier_partialadder_38 (
    .Z(multiplier_partialadder_32_xyout), .Xin(multiplier_partialadder_31_xout),
    .Yin(multiplier_partialadder_37_yout), .Cin(multiplier_partialadder_37_cout),
    .Yout(multiplier_partialadder_38_yout), .Cout(multiplier_partialadder_38_cout),
    .XYout(multiplier_partialadder_38_xyout), .Xout(multiplier_partialadder_38_xout));
  MULTIPLIER_PartialAdder multiplier_partialadder_39 (
    .Z(multiplier_partialadder_33_xyout), .Xin(multiplier_partialadder_32_xout),
    .Yin(multiplier_partialadder_38_yout), .Cin(multiplier_partialadder_38_cout),
    .Yout(multiplier_partialadder_39_yout), .Cout(multiplier_partialadder_39_cout),
    .XYout(multiplier_partialadder_39_xyout), .Xout(multiplier_partialadder_39_xout));
  MULTIPLIER_PartialAdder multiplier_partialadder_40 (
    .Z(multiplier_partialadder_34_xyout), .Xin(multiplier_partialadder_33_xout),
    .Yin(multiplier_partialadder_39_yout), .Cin(multiplier_partialadder_39_cout),
    .Yout(multiplier_partialadder_40_yout), .Cout(multiplier_partialadder_40_cout),
    .XYout(multiplier_partialadder_40_xyout), .Xout(multiplier_partialadder_40_xout));
  MULTIPLIER_PartialAdder multiplier_partialadder_41 (
    .Z(multiplier_partialadder_35_xyout), .Xin(multiplier_partialadder_34_xout),
    .Yin(multiplier_partialadder_40_yout), .Cin(multiplier_partialadder_40_cout),
    .Yout(multiplier_partialadder_41_yout), .Cout(multiplier_partialadder_41_cout),
    .XYout(multiplier_partialadder_41_xyout), .Xout(multiplier_partialadder_41_xout));
  MULTIPLIER_PartialAdder multiplier_partialadder_42 (
    .Z(multiplier_partialaddernot_5_xyout), .Xin(multiplier_partialadder_35_xout),
    .Yin(multiplier_partialadder_41_yout), .Cin(multiplier_partialadder_41_cout),
    .Yout(multiplier_partialadder_42_yout), .Cout(multiplier_partialadder_42_cout),
    .XYout(multiplier_partialadder_42_xyout), .Xout(multiplier_partialadder_42_xout));
  MULTIPLIER_PartialAdderNot multiplier_partialaddernot_6 (
    .Z(multiplier_partialaddernot_5_cout), .Xin(multiplier_partialaddernot_5_xout),
    .Yin(multiplier_partialadder_42_yout), .Cin(multiplier_partialadder_42_cout),
    .Cout(multiplier_partialaddernot_6_cout), .XYout(multiplier_partialaddernot_6_xyout),
    .Xout(multiplier_partialaddernot_6_xout));  // open: Yout
  MULTIPLIER_PartialAdderNot multiplier_partialaddernot_7 (
    .Z(multiplier_partialadder_37_xyout), .Xin(multiplier_partialadder_36_xout), .Yin(A7), .Cin(1'b0),
    .Yout(multiplier_partialaddernot_7_yout), .Cout(multiplier_partialaddernot_7_cout), .XYout(Z7));  // open: Xout
  MULTIPLIER_PartialAdderNot multiplier_partialaddernot_8 (
    .Z(multiplier_partialadder_38_xyout), .Xin(multiplier_partialadder_37_xout),
    .Yin(multiplier_partialaddernot_7_yout), .Cin(multiplier_partialaddernot_7_cout),
    .Yout(multiplier_partialaddernot_8_yout), .Cout(multiplier_partialaddernot_8_cout),
    .XYout(multiplier_partialaddernot_8_xyout));  // open: Xout
  MULTIPLIER_PartialAdderNot multiplier_partialaddernot_9 (
    .Z(multiplier_partialadder_39_xyout), .Xin(multiplier_partialadder_38_xout),
    .Yin(multiplier_partialaddernot_8_yout), .Cin(multiplier_partialaddernot_8_cout),
    .Yout(multiplier_partialaddernot_9_yout), .Cout(multiplier_partialaddernot_9_cout),
    .XYout(multiplier_partialaddernot_9_xyout));  // open: Xout
  MULTIPLIER_PartialAdderNot multiplier_partialaddernot_10 (
    .Z(multiplier_partialadder_40_xyout), .Xin(multiplier_partialadder_39_xout),
    .Yin(multiplier_partialaddernot_9_yout), .Cin(multiplier_partialaddernot_9_cout),
    .Yout(multiplier_partialaddernot_10_yout), .Cout(multiplier_partialaddernot_10_cout),
    .XYout(multiplier_partialaddernot_10_xyout));  // open: Xout
  MULTIPLIER_PartialAdderNot multiplier_partialaddernot_11 (
    .Z(multiplier_partialadder_41_xyout), .Xin(multiplier_partialadder_40_xout),
    .Yin(multiplier_partialaddernot_10_yout), .Cin(multiplier_partialaddernot_10_cout),
    .Yout(multiplier_partialaddernot_11_yout), .Cout(multiplier_partialaddernot_11_cout),
    .XYout(multiplier_partialaddernot_11_xyout));  // open: Xout
  MULTIPLIER_PartialAdderNot multiplier_partialaddernot_12 (
    .Z(multiplier_partialadder_42_xyout), .Xin(multiplier_partialadder_41_xout),
    .Yin(multiplier_partialaddernot_11_yout), .Cin(multiplier_partialaddernot_11_cout),
    .Yout(multiplier_partialaddernot_12_yout), .Cout(multiplier_partialaddernot_12_cout),
    .XYout(multiplier_partialaddernot_12_xyout));  // open: Xout
  MULTIPLIER_PartialAdderNot multiplier_partialaddernot_13 (
    .Z(multiplier_partialaddernot_6_xyout), .Xin(multiplier_partialadder_42_xout),
    .Yin(multiplier_partialaddernot_12_yout), .Cin(multiplier_partialaddernot_12_cout),
    .Yout(multiplier_partialaddernot_13_yout), .Cout(multiplier_partialaddernot_13_cout),
    .XYout(multiplier_partialaddernot_13_xyout));  // open: Xout
  MULTIPLIER_PartialAdder multiplier_partialadder_43 (
    .Z(multiplier_partialaddernot_6_cout), .Xin(multiplier_partialaddernot_6_xout),
    .Yin(multiplier_partialaddernot_13_yout), .Cin(multiplier_partialaddernot_13_cout),
    .Cout(multiplier_partialadder_43_cout), .XYout(multiplier_partialadder_43_xyout));  // open: Yout, Xout
  MULTIPLIER_PartialAdder multiplier_partialadder_44 (
    .Z(1'b1), .Xin(1'b0), .Yin(1'b0), .Cin(multiplier_partialadder_43_cout),
    .XYout(multiplier_partialadder_44_xyout));  // open: Yout, Cout, Xout
  xor xor_1 (xor_1_out, multiplier_partialaddernot_8_xyout, Z7);
  xor xor_2 (xor_2_out, multiplier_partialaddernot_9_xyout, Z7);
  xor xor_3 (xor_3_out, multiplier_partialaddernot_10_xyout, Z7);
  xor xor_4 (xor_4_out, multiplier_partialaddernot_11_xyout, Z7);
  xor xor_5 (xor_5_out, multiplier_partialaddernot_12_xyout, Z7);
  xor xor_6 (xor_6_out, multiplier_partialaddernot_13_xyout, Z7);
  xor xor_7 (xor_7_out, multiplier_partialadder_43_xyout, Z7);
  xor xor_8 (xor_8_out, multiplier_partialadder_44_xyout, Z7);
  or or_1 (OVERFLOW, xor_1_out, xor_2_out, xor_3_out, xor_4_out, xor_5_out, xor_6_out, xor_7_out, xor_8_out);

  // Notes on the sheet:
  //   0
  //   1
  //   2
  //   3
  //   4
  //   5
  //   6
  //   7
  //   8
  //   9
  //   10
  //   11
  //   12
  //   13
  //   14
  //   15
endmodule

module MULTIPLIER_FullAdder (
  input  Cin,
  input  Xin,
  input  Yin,
  output XYout,
  output Cout
);

  wire and_1_out, and_2_out, xor_1_out;

  and and_1 (and_1_out, Xin, Yin);
  xor xor_1 (xor_1_out, Xin, Yin);
  and and_2 (and_2_out, Cin, xor_1_out);
  or or_1 (Cout, and_1_out, and_2_out);
  xor xor_2 (XYout, Cin, xor_1_out);
endmodule

module MULTIPLIER_PartialAdderNot (
  input  Yin,
  input  Cin,
  input  Xin,
  input  Z,
  output XYout,
  output Xout,
  output Yout,
  output Cout
);

  wire nand_1_out;

  nand nand_1 (nand_1_out, Yin, Xin);
  MULTIPLIER_FullAdder multiplier_fulladder_1 (.Xin(nand_1_out), .Yin(Z), .Cin(Cin), .Cout(Cout), .XYout(XYout));

  assign Xout = Xin;
  assign Yout = Yin;
endmodule

module MULTIPLIER_PartialAdder (
  input  Yin,
  input  Cin,
  input  Xin,
  input  Z,
  output XYout,
  output Xout,
  output Yout,
  output Cout
);

  wire and_1_out;

  and and_1 (and_1_out, Yin, Xin);
  MULTIPLIER_FullAdder multiplier_fulladder_1 (.Xin(and_1_out), .Yin(Z), .Cin(Cin), .Cout(Cout), .XYout(XYout));

  assign Xout = Xin;
  assign Yout = Yin;
endmodule

module DIVIDER_FullSubtractor (
  input  A,
  input  B,
  input  Bin,
  input  S,
  output Bout,
  output Z
);

  wire and_1_out, and_2_out, not_1_out, not_2_out, xor_1_out, xor_2_out;

  not not_1 (not_1_out, A);
  xor xor_1 (xor_1_out, A, B);
  and and_1 (and_1_out, not_1_out, B);
  xor xor_2 (xor_2_out, xor_1_out, Bin);
  not not_2 (not_2_out, xor_1_out);
  and and_2 (and_2_out, not_2_out, Bin);
  ALU_MultiplexerX2 alu_multiplexerx2_1 (.S3(S), .D0(A), .D1(xor_2_out), .Z(Z));
  or or_1 (Bout, and_2_out, and_1_out);
endmodule
