// Logisim project Fixed_Point_Multiplier.circ as structural Verilog: 1 circuit, main circuit main
module main (
  input  A0,
  input  A1,
  input  A4,
  input  A5,
  input  A6,
  input  A7,
  input  A2,
  input  A3,
  input  B0,
  input  B1,
  input  B2,
  input  B3,
  input  B4,
  input  B5,
  input  B6,
  input  B7,
  output X0,
  output X1,
  output X2
);

  wire and_2_out, and_3_out, and_4_out, and_5_out, and_6_out, and_7_out, and_8_out, and_9_out, and_10_out,
       and_11_out, and_12_out, and_13_out, and_14_out, and_15_out, and_16_out, and_17_out, and_18_out,
       and_19_out, and_20_out, and_21_out, and_22_out, and_23_out, and_25_out, and_26_out, and_27_out,
       and_28_out, and_29_out, and_30_out, and_31_out, and_32_out, and_33_out, and_34_out, and_35_out,
       and_36_out, and_37_out, and_38_out, or_1_out, or_2_out, or_3_out, or_4_out, or_5_out, or_6_out,
       or_7_out, xor_2_out, xor_3_out, xor_4_out, xor_5_out, xor_6_out, xor_7_out, xor_8_out, xor_9_out,
       xor_10_out, xor_11_out, xor_12_out, xor_13_out, xor_14_out, xor_16_out, xor_17_out, xor_18_out,
       xor_19_out;

  and and_1 (X0, B0, A0);
  and and_2 (and_2_out, B1, A0);
  and and_3 (and_3_out, B0, A1);
  and and_4 (and_4_out, B2, A0);
  and and_5 (and_5_out, B1, A1);
  and and_6 (and_6_out, B3, A0);
  and and_7 (and_7_out, B2, A1);
  and and_8 (and_8_out, B4, A0);
  and and_9 (and_9_out, B3, A1);
  and and_10 (and_10_out, B5, A0);
  and and_11 (and_11_out, B4, A1);
  and and_12 (and_12_out, B6, A0);
  and and_13 (and_13_out, B5, A1);
  and and_14 (and_14_out, B7, A0);
  and and_15 (and_15_out, B6, A1);
  and and_16 (and_16_out, B7, A1);
  xor xor_1 (X1, and_2_out, and_3_out);
  and and_17 (and_17_out, and_2_out, and_3_out);
  and and_18 (and_18_out, and_4_out, and_5_out);
  and and_19 (and_19_out, and_6_out, and_7_out);
  and and_20 (and_20_out, and_8_out, and_9_out);
  and and_21 (and_21_out, and_10_out, and_11_out);
  and and_22 (and_22_out, and_12_out, and_13_out);
  and and_23 (and_23_out, and_14_out, and_15_out);
  // AND_Gate and_24 has open pins: in0=or_6_out, in1=and_16_out, out=open
  xor xor_2 (xor_2_out, and_4_out, and_5_out);
  xor xor_3 (xor_3_out, and_6_out, and_7_out);
  xor xor_4 (xor_4_out, and_8_out, and_9_out);
  xor xor_5 (xor_5_out, and_10_out, and_11_out);
  xor xor_6 (xor_6_out, and_12_out, and_13_out);
  xor xor_7 (xor_7_out, and_14_out, and_15_out);
  xor xor_8 (xor_8_out, or_6_out, and_16_out);
  xor xor_9 (xor_9_out, and_17_out, xor_2_out);
  and and_25 (and_25_out, and_17_out, xor_2_out);
  xor xor_10 (xor_10_out, xor_3_out, or_1_out);
  and and_26 (and_26_out, xor_3_out, or_1_out);
  xor xor_11 (xor_11_out, xor_4_out, or_2_out);
  and and_27 (and_27_out, xor_4_out, or_2_out);
  xor xor_12 (xor_12_out, xor_5_out, or_3_out);
  and and_28 (and_28_out, xor_5_out, or_3_out);
  xor xor_13 (xor_13_out, xor_6_out, or_4_out);
  and and_29 (and_29_out, xor_6_out, or_4_out);
  xor xor_14 (xor_14_out, xor_7_out, or_5_out);
  and and_30 (and_30_out, xor_7_out, or_5_out);
  or or_1 (or_1_out, and_25_out, and_18_out);
  or or_2 (or_2_out, and_26_out, and_19_out);
  or or_3 (or_3_out, and_27_out, and_20_out);
  or or_4 (or_4_out, and_28_out, and_21_out);
  or or_5 (or_5_out, and_29_out, and_22_out);
  or or_6 (or_6_out, and_30_out, and_23_out);
  and and_31 (and_31_out, B0, A2);
  and and_32 (and_32_out, B1, A2);
  and and_33 (and_33_out, B2, A2);
  and and_34 (and_34_out, xor_9_out, and_31_out);
  xor xor_15 (X2, and_31_out, xor_9_out);
  xor xor_16 (xor_16_out, and_32_out, xor_10_out);
  and and_35 (and_35_out, and_32_out, xor_10_out);
  xor xor_17 (xor_17_out, and_33_out, xor_11_out);
  and and_36 (and_36_out, and_33_out, xor_11_out);
  and and_37 (and_37_out, xor_16_out, and_34_out);
  and and_38 (and_38_out, xor_17_out, or_7_out);
  xor xor_18 (xor_18_out, xor_16_out, and_34_out);
  xor xor_19 (xor_19_out, xor_17_out, or_7_out);
  or or_7 (or_7_out, and_37_out, and_35_out);
  // OR_Gate or_8 has open pins: in0=and_38_out, in1=and_36_out, out=open
endmodule
